// Logisim project CPUProto1.circ as structural Verilog: 2 circuits, main circuit One_Bit_ALU
module One_Bit_ALU (
  input  Subt,
  input  C_In,
  input  A,
  input  B,
  input  [2:0] Selector,
  input  Less,
  output Result,
  output C_Out,
  output Set
);

  wire and_1_out, nor_1_out, or_1_out, xor_1_out, xor_2_out;

  and and_1 (and_1_out, A, B);
  or or_1 (or_1_out, A, B);
  xor xor_1 (xor_1_out, A, B);
  nor nor_1 (nor_1_out, A, B);
  xor xor_2 (xor_2_out, B, Subt);
  Adder #(.width(1)) adder_1 (.a(A), .b(xor_2_out), .out(Set), .cin(C_In), .cout(C_Out));
  Multiplexer #(.select(3)) multiplexer_1 (
    .in0(and_1_out), .in1(or_1_out), .in2(xor_1_out), .in3(nor_1_out), .in4(Set), .in5(Less), .out(Result),
    .sel(Selector));  // open: in6, in7
endmodule

module ALU (
  input  [7:0] A,
  input  [2:0] Selector,
  input  Subt,
  input  [7:0] B,
  output [7:0] Result,
  output Zero
);

  wire one_bit_alu_1_c_out, one_bit_alu_2_c_out, one_bit_alu_3_c_out, one_bit_alu_4_c_out,
       one_bit_alu_5_c_out, one_bit_alu_6_c_out, one_bit_alu_7_c_out, one_bit_alu_8_set;

  One_Bit_ALU one_bit_alu_1 (
    .Subt(Subt), .C_In(Subt), .A(A[0]), .B(B[0]), .Selector(Selector), .Less(one_bit_alu_8_set),
    .Result(Result[0]), .C_Out(one_bit_alu_1_c_out));  // open: Set
  One_Bit_ALU one_bit_alu_2 (
    .Subt(Subt), .C_In(one_bit_alu_1_c_out), .A(A[1]), .B(B[1]), .Selector(Selector), .Less(1'b0),
    .Result(Result[1]), .C_Out(one_bit_alu_2_c_out));  // open: Set
  One_Bit_ALU one_bit_alu_3 (
    .Subt(Subt), .C_In(one_bit_alu_2_c_out), .A(A[2]), .B(B[2]), .Selector(Selector), .Less(1'b0),
    .Result(Result[2]), .C_Out(one_bit_alu_3_c_out));  // open: Set
  One_Bit_ALU one_bit_alu_4 (
    .Subt(Subt), .C_In(one_bit_alu_3_c_out), .A(A[3]), .B(B[3]), .Selector(Selector), .Less(1'b0),
    .Result(Result[3]), .C_Out(one_bit_alu_4_c_out));  // open: Set
  One_Bit_ALU one_bit_alu_5 (
    .Subt(Subt), .C_In(one_bit_alu_4_c_out), .A(A[4]), .B(B[4]), .Selector(Selector), .Less(1'b0),
    .Result(Result[4]), .C_Out(one_bit_alu_5_c_out));  // open: Set
  One_Bit_ALU one_bit_alu_6 (
    .Subt(Subt), .C_In(one_bit_alu_5_c_out), .A(A[5]), .B(B[5]), .Selector(Selector), .Less(1'b0),
    .Result(Result[5]), .C_Out(one_bit_alu_6_c_out));  // open: Set
  One_Bit_ALU one_bit_alu_7 (
    .Subt(Subt), .C_In(one_bit_alu_6_c_out), .A(A[6]), .B(B[6]), .Selector(Selector), .Less(1'b0),
    .Result(Result[6]), .C_Out(one_bit_alu_7_c_out));  // open: Set
  One_Bit_ALU one_bit_alu_8 (
    .Subt(Subt), .C_In(one_bit_alu_7_c_out), .A(A[7]), .B(B[7]), .Selector(Selector), .Less(1'b0),
    .Result(Result[7]), .Set(one_bit_alu_8_set));  // open: C_Out
  nor nor_1 (Zero, Result[0], Result[1], Result[2], Result[3], Result[4], Result[5], Result[6], Result[7]);

  // Notes on the sheet:
  //   Inputs
  //   Enable to Subtract Instead of add
  //   Select Operations: 100 = ADD
  //   End Result
  //   Final Result is 0
endmodule
